// Logisim project aaaaa.circ as structural Verilog
module main (
  output [15:0] out_1,
  output [15:0] out_2
);

  wire and_1_out, and_3_out, and_9_out, avail, button_2_out, button_3_out, button_4_out, button_5_out,
       button_6_out, button_en, button_out, cdm_16_1_p3, clk, clr_tty1, clr_tty1_io, clr_tty2, clr_tty2_io,
       clr_tty3, clr_tty3_io, dmplxr, io_en, keyboard_1_avail, mem, not_1_out, r_w_prime, random,
       read_en_keyboard, word, write_en_tty1, write_en_tty1_io, write_en_tty2, write_en_tty2_io,
       write_en_tty3, write_en_tty3_io;
  wire [6:0] keyboard_1_data;
  wire [7:0] random_1_out;
  wire [9:0] controller_bot_1_out1, controller_bot_1_out2, controller_bot_1_out3, controller_bot_1_out4,
       controller_bot_1_out5, controller_bot_1_out6, controller_bot_1_out7, controller_bot_1_out8,
       controller_bot_1_out9, controller_bot_1_out10, controller_gamer_1_out1, controller_gamer_1_out2,
       controller_gamer_1_out3, controller_gamer_1_out4, controller_gamer_1_out5, controller_gamer_1_out6,
       controller_gamer_1_out7, controller_gamer_1_out8, controller_gamer_1_out9, controller_gamer_1_out10;
  wire [13:0] controller_bot_1_out1_3, controller_bot_1_out2_3, controller_bot_1_out3_3,
       controller_bot_1_out4_3, controller_bot_1_out5_3, controller_bot_1_out6_3, controller_bot_1_out7_3,
       controller_bot_1_out8_3, controller_bot_1_out9_3, controller_bot_1_out10_3, controller_gamer_1_out1_3,
       controller_gamer_1_out2_3, controller_gamer_1_out3_3, controller_gamer_1_out4_3,
       controller_gamer_1_out5_3, controller_gamer_1_out6_3, controller_gamer_1_out7_3,
       controller_gamer_1_out8_3, controller_gamer_1_out9_3, controller_gamer_1_out10_3;
  wire [15:0] addr, bit_extender_1_out, bit_extender_2_out, bit_extender_3_out, controller_bot_1_out1_2,
       controller_bot_1_out2_2, controller_bot_1_out3_2, controller_bot_1_out4_2, controller_bot_1_out5_2,
       controller_bot_1_out6_2, controller_bot_1_out7_2, controller_bot_1_out8_2, controller_bot_1_out9_2,
       controller_bot_1_out10_2, controller_gamer_1_out1_2, controller_gamer_1_out2_2,
       controller_gamer_1_out3_2, controller_gamer_1_out4_2, controller_gamer_1_out5_2,
       controller_gamer_1_out6_2, controller_gamer_1_out7_2, controller_gamer_1_out8_2,
       controller_gamer_1_out9_2, controller_gamer_1_out10_2, data, in, out;

  Clock clock_1 (.out(clk));
  horizont_lines horizont_lines_1 ();
  controller_bot controller_bot_1 (
    .clk(clk), .data(data), .out1(controller_bot_1_out1), .out2(controller_bot_1_out2),
    .out3(controller_bot_1_out3), .out4(controller_bot_1_out4), .out5(controller_bot_1_out5),
    .out6(controller_bot_1_out6), .out7(controller_bot_1_out7), .out8(controller_bot_1_out8),
    .out9(controller_bot_1_out9), .out10(controller_bot_1_out10), .in_1(addr), .r_w_prime(r_w_prime),
    .mem(mem), .out1_2(controller_bot_1_out1_2), .out1_3(controller_bot_1_out1_3),
    .out2_2(controller_bot_1_out2_2), .out2_3(controller_bot_1_out2_3), .out3_2(controller_bot_1_out3_2),
    .out3_3(controller_bot_1_out3_3), .out4_2(controller_bot_1_out4_2), .out4_3(controller_bot_1_out4_3),
    .out5_2(controller_bot_1_out5_2), .out5_3(controller_bot_1_out5_3), .out6_2(controller_bot_1_out6_2),
    .out6_3(controller_bot_1_out6_3), .out7_2(controller_bot_1_out7_2), .out7_3(controller_bot_1_out7_3),
    .out8_2(controller_bot_1_out8_2), .out8_3(controller_bot_1_out8_3), .out9_2(controller_bot_1_out9_2),
    .out9_3(controller_bot_1_out9_3), .out10_2(controller_bot_1_out10_2), .out10_3(controller_bot_1_out10_3));
  DotMatrix #(.inputtype("row"), .matrixcols(16), .matrixrows(10)) dotmatrix_1 (
    .row0(controller_bot_1_out1_2), .row1(controller_bot_1_out2_2), .row2(controller_bot_1_out3_2),
    .row3(controller_bot_1_out4_2), .row4(controller_bot_1_out5_2), .row5(controller_bot_1_out6_2),
    .row6(controller_bot_1_out7_2), .row7(controller_bot_1_out8_2), .row8(controller_bot_1_out9_2),
    .row9(controller_bot_1_out10_2));
  DotMatrix #(.inputtype("row"), .matrixcols(14), .matrixrows(11)) dotmatrix_2 (
    .row0(controller_bot_1_out1_3), .row1(controller_bot_1_out2_3), .row2(controller_bot_1_out3_3),
    .row3(controller_bot_1_out4_3), .row4(controller_bot_1_out5_3), .row5(controller_bot_1_out6_3),
    .row6(controller_bot_1_out7_3), .row7(controller_bot_1_out8_3), .row8(controller_bot_1_out9_3),
    .row9(controller_bot_1_out10_3));  // open: row10
  // Debugger debugger_1: pin names not known
  DotMatrix #(.inputtype("row"), .matrixcols(10), .matrixrows(11)) dotmatrix_3 (
    .row1(controller_bot_1_out1), .row2(controller_bot_1_out2), .row3(controller_bot_1_out3),
    .row4(controller_bot_1_out4), .row5(controller_bot_1_out5), .row6(controller_bot_1_out6),
    .row7(controller_bot_1_out7), .row8(controller_bot_1_out8), .row9(controller_bot_1_out9),
    .row10(controller_bot_1_out10));  // open: row0
  TTY #(.rows(2), .cols(25)) tty_1 (.data(data[6:0]), .clk(clk), .we(write_en_tty3_io), .clr(clr_tty3_io));
  DotMatrix #(.inputtype("row"), .matrixcols(10), .matrixrows(11)) dotmatrix_4 (
    .row1(controller_gamer_1_out1), .row2(controller_gamer_1_out2), .row3(controller_gamer_1_out3),
    .row4(controller_gamer_1_out4), .row5(controller_gamer_1_out5), .row6(controller_gamer_1_out6),
    .row7(controller_gamer_1_out7), .row8(controller_gamer_1_out8), .row9(controller_gamer_1_out9),
    .row10(controller_gamer_1_out10));  // open: row0
  controller_gamer controller_gamer_1 (
    .in_1(addr), .clk(clk), .r_w_prime(r_w_prime), .data(data), .out1(controller_gamer_1_out1),
    .out2(controller_gamer_1_out2), .out3(controller_gamer_1_out3), .out4(controller_gamer_1_out4),
    .out5(controller_gamer_1_out5), .out6(controller_gamer_1_out6), .out7(controller_gamer_1_out7),
    .out8(controller_gamer_1_out8), .out9(controller_gamer_1_out9), .out10(controller_gamer_1_out10),
    .mem(mem), .out1_3(controller_gamer_1_out1_3), .out2_3(controller_gamer_1_out2_3),
    .out3_3(controller_gamer_1_out3_3), .out4_3(controller_gamer_1_out4_3),
    .out5_3(controller_gamer_1_out5_3), .out6_3(controller_gamer_1_out6_3),
    .out7_3(controller_gamer_1_out7_3), .out8_3(controller_gamer_1_out8_3),
    .out9_3(controller_gamer_1_out9_3), .out10_3(controller_gamer_1_out10_3),
    .out1_2(controller_gamer_1_out1_2), .out2_2(controller_gamer_1_out2_2),
    .out3_2(controller_gamer_1_out3_2), .out4_2(controller_gamer_1_out4_2),
    .out5_2(controller_gamer_1_out5_2), .out6_2(controller_gamer_1_out6_2),
    .out7_2(controller_gamer_1_out7_2), .out8_2(controller_gamer_1_out8_2),
    .out9_2(controller_gamer_1_out9_2), .out10_2(controller_gamer_1_out10_2));
  DotMatrix #(.inputtype("row"), .matrixcols(14), .matrixrows(11)) dotmatrix_5 (
    .row0(controller_gamer_1_out1_3), .row1(controller_gamer_1_out2_3), .row2(controller_gamer_1_out3_3),
    .row3(controller_gamer_1_out4_3), .row4(controller_gamer_1_out5_3), .row5(controller_gamer_1_out6_3),
    .row6(controller_gamer_1_out7_3), .row7(controller_gamer_1_out8_3), .row8(controller_gamer_1_out9_3),
    .row9(controller_gamer_1_out10_3));  // open: row10
  DotMatrix #(.inputtype("row"), .matrixcols(16), .matrixrows(10)) dotmatrix_6 (
    .row0(controller_gamer_1_out1_2), .row1(controller_gamer_1_out2_2), .row2(controller_gamer_1_out3_2),
    .row3(controller_gamer_1_out4_2), .row4(controller_gamer_1_out5_2), .row5(controller_gamer_1_out6_2),
    .row6(controller_gamer_1_out7_2), .row7(controller_gamer_1_out8_2), .row8(controller_gamer_1_out9_2),
    .row9(controller_gamer_1_out10_2));
  assign data = button_en ? out_2 : 16'bz;  // Controlled_Buffer controlled_buffer_1
  Button button (.out(button_out));
  Button button_2 (.out(button_2_out));
  buttons buttons_1 (
    .left(button_3_out), .up(button_2_out), .right(button_4_out), .down(button_5_out), .turn(button_out),
    .fire_place(button_6_out), .out_8(out_2), .clk(clk));
  Button button_3 (.out(button_3_out));
  Button button_4 (.out(button_4_out));
  Button button_5 (.out(button_5_out));
  Button button_6 (.out(button_6_out));
  Comparator #(.width(16), .mode("unsigned")) comparator_1 (.a(addr), .b(16'h8048), .eq(button_en));  // open: gt, lt
  Comparator #(.width(16), .mode("unsigned")) comparator_2 (.a(addr), .b(16'h800e), .eq(clr_tty3));  // open: gt, lt
  Comparator #(.width(16), .mode("unsigned")) comparator_3 (
    .a(addr), .b(16'h800c), .eq(write_en_tty3));  // open: gt, lt
  Comparator #(.width(16), .mode("unsigned")) comparator_4 (.a(addr), .b(16'h800a), .eq(random));  // open: gt, lt
  Comparator #(.width(16), .mode("unsigned")) comparator_5 (.a(addr), .b(16'h8008), .eq(clr_tty2));  // open: gt, lt
  Comparator #(.width(16), .mode("unsigned")) comparator_6 (.a(addr), .b(16'h8006), .eq(clr_tty1));  // open: gt, lt
  Comparator #(.width(16), .mode("unsigned")) comparator_7 (.a(addr), .b(16'h8005), .eq(avail));  // open: gt, lt
  Comparator #(.width(16), .mode("unsigned")) comparator_8 (
    .a(addr), .b(16'h8004), .eq(read_en_keyboard));  // open: gt, lt
  Comparator #(.width(16), .mode("unsigned")) comparator_9 (
    .a(addr), .b(16'h8002), .eq(write_en_tty2));  // open: gt, lt
  Comparator #(.width(16), .mode("unsigned")) comparator_10 (
    .a(addr), .b(16'h8000), .eq(write_en_tty1));  // open: gt, lt
  // CdM_16 cdm_16_1: pin names not known; wires that end beside it: clk, out_1, cdm_16_1_p3, cdm_16_1_p3, mem, r_w_prime, word, addr, out, in
  assign data = not_1_out ? out : 16'bz;  // Controlled_Buffer controlled_buffer_2
  not not_1 (not_1_out, r_w_prime);
  assign in = r_w_prime ? data : 16'bz;  // Controlled_Buffer controlled_buffer_3
  Keyboard #(.trigger("falling")) keyboard_1 (
    .clk(clk), .re(and_1_out), .avail(keyboard_1_avail), .data(keyboard_1_data));  // open: clr
  and and_1 (and_1_out, io_en, r_w_prime, read_en_keyboard);
  assign bit_extender_1_out = {{15{1'b0}}, keyboard_1_avail};  // Bit_Extender bit_extender_1
  and and_2 (write_en_tty1_io, write_en_tty1, ~r_w_prime, io_en);  // AND_Gate
  assign bit_extender_2_out = {{9{1'b0}}, keyboard_1_data};  // Bit_Extender bit_extender_2
  assign data = and_1_out ? bit_extender_2_out : 16'bz;  // Controlled_Buffer controlled_buffer_4
  assign data = and_3_out ? bit_extender_1_out : 16'bz;  // Controlled_Buffer controlled_buffer_5
  and and_3 (and_3_out, io_en, r_w_prime, avail);
  and and_4 (clr_tty1_io, clr_tty1, r_w_prime, io_en);
  and and_5 (write_en_tty2_io, write_en_tty2, ~r_w_prime, io_en);  // AND_Gate
  and and_6 (io_en, addr[15], mem);
  and and_7 (dmplxr, ~addr[15], mem);  // AND_Gate
  and and_8 (clr_tty2_io, clr_tty2, r_w_prime, io_en);
  assign bit_extender_3_out = {{8{1'b0}}, random_1_out};  // Bit_Extender bit_extender_3
  Random random_1 (.clk(clk), .next(random), .out(random_1_out));  // open: clr
  and and_9 (and_9_out, io_en, r_w_prime, random);
  assign data = and_9_out ? bit_extender_3_out : 16'bz;  // Controlled_Buffer controlled_buffer_6
  and and_10 (write_en_tty3_io, write_en_tty3, ~r_w_prime, io_en);  // AND_Gate
  // RAM ram_1: pin names not known; wires that end beside it: addr, word, dmplxr, clk, r_w_prime, data
  and and_11 (clr_tty3_io, clr_tty3, r_w_prime, io_en);

  // Other names for the same wires on the sheet: data0_6[6:0] = data[6:0]

  // Notes on the sheet:
  //   8016 - misses
  //   805c - hits
  //   bot - 8070 - move
  //   8048 - missts
  //   8086 - hits
  //   ПОЛЕ ВРАГА
  //   gamer - 8034 - move
  //   80a2
  //   ПОЛЕ ИГРОКА
endmodule

module controller_bot (
  input  [15:0] in_1,
  input  [15:0] data,
  input  clk,
  input  r_w_prime,
  input  mem,
  output [9:0] out1,
  output [15:0] out1_2,
  output [13:0] out1_3,
  output [9:0] out2,
  output [15:0] out2_2,
  output [13:0] out2_3,
  output [9:0] out3,
  output [15:0] out3_2,
  output [13:0] out3_3,
  output [9:0] out4,
  output [15:0] out4_2,
  output [13:0] out4_3,
  output [9:0] out5,
  output [15:0] out5_2,
  output [13:0] out5_3,
  output [9:0] out6,
  output [15:0] out6_2,
  output [13:0] out6_3,
  output [9:0] out7,
  output [15:0] out7_2,
  output [13:0] out7_3,
  output [9:0] out8,
  output [15:0] out8_2,
  output [13:0] out8_3,
  output [9:0] out9,
  output [15:0] out9_2,
  output [13:0] out9_3,
  output [9:0] out10,
  output [15:0] out10_2,
  output [13:0] out10_3
);

  wire and_1_out, and_2_out, and_3_out, and_4_out, and_5_out, and_6_out, and_7_out, and_8_out, and_9_out,
       and_10_out, and_11_out, and_12_out, and_13_out, and_14_out, and_15_out, and_16_out, and_17_out,
       and_18_out, and_19_out, and_20_out, and_21_out, and_22_out, and_23_out, and_24_out, and_25_out,
       and_26_out, and_27_out, and_28_out, and_29_out, and_30_out, comparator_1_eq, comparator_2_eq,
       comparator_3_eq, comparator_4_eq, comparator_5_eq, comparator_6_eq, comparator_7_eq, comparator_8_eq,
       comparator_9_eq, comparator_10_eq, comparator_11_eq, comparator_12_eq, comparator_13_eq,
       comparator_14_eq, comparator_15_eq, comparator_16_eq, comparator_17_eq, comparator_18_eq,
       comparator_19_eq, comparator_20_eq, comparator_21_eq, comparator_22_eq, comparator_23_eq,
       comparator_24_eq, comparator_25_eq, comparator_26_eq, comparator_27_eq, comparator_28_eq,
       comparator_29_eq, comparator_30_eq, w;
  wire [15:10] register_1_q, register_2_q, register_3_q, register_4_q, register_5_q, register_6_q,
       register_7_q, register_8_q, register_9_q, register_10_q;
  wire [15:14] register_11_q, register_12_q, register_13_q, register_14_q, register_15_q, register_16_q,
       register_17_q, register_18_q, register_19_q, register_20_q;

  Comparator #(.width(16), .mode("unsigned")) comparator_1 (
    .a(in_1), .b(16'h8016), .eq(comparator_1_eq));  // open: gt, lt
  Comparator #(.width(16), .mode("unsigned")) comparator_2 (
    .a(in_1), .b(16'h8018), .eq(comparator_2_eq));  // open: gt, lt
  Comparator #(.width(16), .mode("unsigned")) comparator_3 (
    .a(in_1), .b(16'h801a), .eq(comparator_3_eq));  // open: gt, lt
  Comparator #(.width(16), .mode("unsigned")) comparator_4 (
    .a(in_1), .b(16'h801c), .eq(comparator_4_eq));  // open: gt, lt
  Comparator #(.width(16), .mode("unsigned")) comparator_5 (
    .a(in_1), .b(16'h801e), .eq(comparator_5_eq));  // open: gt, lt
  Comparator #(.width(16), .mode("unsigned")) comparator_6 (
    .a(in_1), .b(16'h8020), .eq(comparator_6_eq));  // open: gt, lt
  Comparator #(.width(16), .mode("unsigned")) comparator_7 (
    .a(in_1), .b(16'h8022), .eq(comparator_7_eq));  // open: gt, lt
  Comparator #(.width(16), .mode("unsigned")) comparator_8 (
    .a(in_1), .b(16'h8024), .eq(comparator_8_eq));  // open: gt, lt
  Comparator #(.width(16), .mode("unsigned")) comparator_9 (
    .a(in_1), .b(16'h8026), .eq(comparator_9_eq));  // open: gt, lt
  Comparator #(.width(16), .mode("unsigned")) comparator_10 (
    .a(in_1), .b(16'h8028), .eq(comparator_10_eq));  // open: gt, lt
  not not_1 (w, r_w_prime);
  and and_1 (and_1_out, comparator_1_eq, mem, w);
  and and_2 (and_2_out, comparator_2_eq, mem, w);
  and and_3 (and_3_out, comparator_3_eq, mem, w);
  and and_4 (and_4_out, comparator_4_eq, mem, w);
  and and_5 (and_5_out, comparator_5_eq, mem, w);
  and and_6 (and_6_out, comparator_6_eq, mem, w);
  and and_7 (and_7_out, comparator_7_eq, mem, w);
  and and_8 (and_8_out, comparator_8_eq, mem, w);
  and and_9 (and_9_out, comparator_9_eq, mem, w);
  and and_10 (and_10_out, comparator_10_eq, mem, w);
  Register #(.width(16)) register_1 (.D(data), .en(and_1_out), .Q({register_1_q, out1}), .clk(clk));  // open: clr
  Register #(.width(16)) register_2 (.D(data), .en(and_2_out), .Q({register_2_q, out2}), .clk(clk));  // open: clr
  Register #(.width(16)) register_3 (.D(data), .en(and_3_out), .Q({register_3_q, out3}), .clk(clk));  // open: clr
  Register #(.width(16)) register_4 (.D(data), .en(and_4_out), .Q({register_4_q, out4}), .clk(clk));  // open: clr
  Register #(.width(16)) register_5 (.D(data), .en(and_5_out), .Q({register_5_q, out5}), .clk(clk));  // open: clr
  Register #(.width(16)) register_6 (.D(data), .en(and_6_out), .Q({register_6_q, out6}), .clk(clk));  // open: clr
  Register #(.width(16)) register_7 (.D(data), .en(and_7_out), .Q({register_7_q, out7}), .clk(clk));  // open: clr
  Register #(.width(16)) register_8 (.D(data), .en(and_8_out), .Q({register_8_q, out8}), .clk(clk));  // open: clr
  Register #(.width(16)) register_9 (.D(data), .en(and_9_out), .Q({register_9_q, out9}), .clk(clk));  // open: clr
  Register #(.width(16)) register_10 (.D(data), .en(and_10_out), .Q({register_10_q, out10}), .clk(clk));  // open: clr
  Comparator #(.width(16), .mode("unsigned")) comparator_11 (
    .a(in_1), .b(16'h805c), .eq(comparator_11_eq));  // open: gt, lt
  Comparator #(.width(16), .mode("unsigned")) comparator_12 (
    .a(in_1), .b(16'h805e), .eq(comparator_12_eq));  // open: gt, lt
  Comparator #(.width(16), .mode("unsigned")) comparator_13 (
    .a(in_1), .b(16'h8060), .eq(comparator_13_eq));  // open: gt, lt
  Comparator #(.width(16), .mode("unsigned")) comparator_14 (
    .a(in_1), .b(16'h8062), .eq(comparator_14_eq));  // open: gt, lt
  Comparator #(.width(16), .mode("unsigned")) comparator_15 (
    .a(in_1), .b(16'h8064), .eq(comparator_15_eq));  // open: gt, lt
  Comparator #(.width(16), .mode("unsigned")) comparator_16 (
    .a(in_1), .b(16'h8066), .eq(comparator_16_eq));  // open: gt, lt
  Comparator #(.width(16), .mode("unsigned")) comparator_17 (
    .a(in_1), .b(16'h8068), .eq(comparator_17_eq));  // open: gt, lt
  Comparator #(.width(16), .mode("unsigned")) comparator_18 (
    .a(in_1), .b(16'h806a), .eq(comparator_18_eq));  // open: gt, lt
  Comparator #(.width(16), .mode("unsigned")) comparator_19 (
    .a(in_1), .b(16'h806c), .eq(comparator_19_eq));  // open: gt, lt
  Comparator #(.width(16), .mode("unsigned")) comparator_20 (
    .a(in_1), .b(16'h806e), .eq(comparator_20_eq));  // open: gt, lt
  and and_11 (and_11_out, comparator_11_eq, mem, w);
  and and_12 (and_12_out, comparator_12_eq, mem, w);
  and and_13 (and_13_out, comparator_13_eq, mem, w);
  and and_14 (and_14_out, comparator_14_eq, mem, w);
  and and_15 (and_15_out, comparator_15_eq, mem, w);
  and and_16 (and_16_out, comparator_16_eq, mem, w);
  and and_17 (and_17_out, comparator_17_eq, mem, w);
  and and_18 (and_18_out, comparator_18_eq, mem, w);
  and and_19 (and_19_out, comparator_19_eq, mem, w);
  and and_20 (and_20_out, comparator_20_eq, mem, w);
  Register #(.width(16), .trigger("falling")) register_11 (
    .D(data), .en(and_11_out), .Q({register_11_q, out1_3}), .clk(clk));  // open: clr
  Register #(.width(16), .trigger("falling")) register_12 (
    .D(data), .en(and_12_out), .Q({register_12_q, out2_3}), .clk(clk));  // open: clr
  Register #(.width(16), .trigger("falling")) register_13 (
    .D(data), .en(and_13_out), .Q({register_13_q, out3_3}), .clk(clk));  // open: clr
  Register #(.width(16), .trigger("falling")) register_14 (
    .D(data), .en(and_14_out), .Q({register_14_q, out4_3}), .clk(clk));  // open: clr
  Register #(.width(16), .trigger("falling")) register_15 (
    .D(data), .en(and_15_out), .Q({register_15_q, out5_3}), .clk(clk));  // open: clr
  Register #(.width(16), .trigger("falling")) register_16 (
    .D(data), .en(and_16_out), .Q({register_16_q, out6_3}), .clk(clk));  // open: clr
  Register #(.width(16), .trigger("falling")) register_17 (
    .D(data), .en(and_17_out), .Q({register_17_q, out7_3}), .clk(clk));  // open: clr
  Register #(.width(16), .trigger("falling")) register_18 (
    .D(data), .en(and_18_out), .Q({register_18_q, out8_3}), .clk(clk));  // open: clr
  Register #(.width(16), .trigger("falling")) register_19 (
    .D(data), .en(and_19_out), .Q({register_19_q, out9_3}), .clk(clk));  // open: clr
  Register #(.width(16), .trigger("falling")) register_20 (
    .D(data), .en(and_20_out), .Q({register_20_q, out10_3}), .clk(clk));  // open: clr
  Comparator #(.width(16), .mode("unsigned")) comparator_21 (
    .a(in_1), .b(16'h8070), .eq(comparator_21_eq));  // open: gt, lt
  Comparator #(.width(16), .mode("unsigned")) comparator_22 (
    .a(in_1), .b(16'h8072), .eq(comparator_22_eq));  // open: gt, lt
  Comparator #(.width(16), .mode("unsigned")) comparator_23 (
    .a(in_1), .b(16'h8074), .eq(comparator_23_eq));  // open: gt, lt
  Comparator #(.width(16), .mode("unsigned")) comparator_24 (
    .a(in_1), .b(16'h8076), .eq(comparator_24_eq));  // open: gt, lt
  Comparator #(.width(16), .mode("unsigned")) comparator_25 (
    .a(in_1), .b(16'h8078), .eq(comparator_25_eq));  // open: gt, lt
  Comparator #(.width(16), .mode("unsigned")) comparator_26 (
    .a(in_1), .b(16'h807a), .eq(comparator_26_eq));  // open: gt, lt
  Comparator #(.width(16), .mode("unsigned")) comparator_27 (
    .a(in_1), .b(16'h807c), .eq(comparator_27_eq));  // open: gt, lt
  Comparator #(.width(16), .mode("unsigned")) comparator_28 (
    .a(in_1), .b(16'h807e), .eq(comparator_28_eq));  // open: gt, lt
  Comparator #(.width(16), .mode("unsigned")) comparator_29 (
    .a(in_1), .b(16'h8080), .eq(comparator_29_eq));  // open: gt, lt
  Comparator #(.width(16), .mode("unsigned")) comparator_30 (
    .a(in_1), .b(16'h8082), .eq(comparator_30_eq));  // open: gt, lt
  Register #(.width(16), .trigger("falling")) register_21 (
    .D(data), .en(and_21_out), .Q(out1_2), .clk(clk));  // open: clr
  and and_21 (and_21_out, comparator_21_eq, mem, w);
  Register #(.width(16), .trigger("falling")) register_22 (
    .D(data), .en(and_22_out), .Q(out2_2), .clk(clk));  // open: clr
  and and_22 (and_22_out, comparator_22_eq, mem, w);
  Register #(.width(16), .trigger("falling")) register_23 (
    .D(data), .en(and_23_out), .Q(out3_2), .clk(clk));  // open: clr
  and and_23 (and_23_out, comparator_23_eq, mem, w);
  Register #(.width(16), .trigger("falling")) register_24 (
    .D(data), .en(and_24_out), .Q(out4_2), .clk(clk));  // open: clr
  and and_24 (and_24_out, comparator_24_eq, mem, w);
  Register #(.width(16), .trigger("falling")) register_25 (
    .D(data), .en(and_25_out), .Q(out5_2), .clk(clk));  // open: clr
  and and_25 (and_25_out, comparator_25_eq, mem, w);
  Register #(.width(16), .trigger("falling")) register_26 (
    .D(data), .en(and_26_out), .Q(out6_2), .clk(clk));  // open: clr
  and and_26 (and_26_out, comparator_26_eq, mem, w);
  Register #(.width(16), .trigger("falling")) register_27 (
    .D(data), .en(and_27_out), .Q(out7_2), .clk(clk));  // open: clr
  and and_27 (and_27_out, comparator_27_eq, mem, w);
  Register #(.width(16), .trigger("falling")) register_28 (
    .D(data), .en(and_28_out), .Q(out8_2), .clk(clk));  // open: clr
  and and_28 (and_28_out, comparator_28_eq, mem, w);
  Register #(.width(16), .trigger("falling")) register_29 (
    .D(data), .en(and_29_out), .Q(out9_2), .clk(clk));  // open: clr
  and and_29 (and_29_out, comparator_29_eq, mem, w);
  Register #(.width(16), .trigger("falling")) register_30 (
    .D(data), .en(and_30_out), .Q(out10_2), .clk(clk));  // open: clr
  and and_30 (and_30_out, comparator_30_eq, mem, w);

  // Other names for the same wires on the sheet: addr[15:0] = in_1
endmodule

module controller_gamer (
  input  [15:0] in_1,
  input  [15:0] data,
  input  clk,
  input  r_w_prime,
  input  mem,
  output [9:0] out1,
  output [15:0] out1_2,
  output [13:0] out1_3,
  output [9:0] out2,
  output [15:0] out2_2,
  output [13:0] out2_3,
  output [9:0] out3,
  output [15:0] out3_2,
  output [13:0] out3_3,
  output [9:0] out4,
  output [15:0] out4_2,
  output [13:0] out4_3,
  output [9:0] out5,
  output [15:0] out5_2,
  output [13:0] out5_3,
  output [9:0] out6,
  output [15:0] out6_2,
  output [13:0] out6_3,
  output [9:0] out7,
  output [15:0] out7_2,
  output [13:0] out7_3,
  output [9:0] out8,
  output [15:0] out8_2,
  output [13:0] out8_3,
  output [9:0] out9,
  output [15:0] out9_2,
  output [13:0] out9_3,
  output [9:0] out10,
  output [15:0] out10_2,
  output [13:0] out10_3
);

  wire and_1_out, and_2_out, and_3_out, and_4_out, and_5_out, and_6_out, and_7_out, and_8_out, and_9_out,
       and_10_out, and_11_out, and_12_out, and_13_out, and_14_out, and_15_out, and_16_out, and_17_out,
       and_18_out, and_19_out, and_20_out, and_21_out, and_22_out, and_23_out, and_24_out, and_25_out,
       and_26_out, and_27_out, and_28_out, and_29_out, and_30_out, comparator_1_eq, comparator_2_eq,
       comparator_3_eq, comparator_4_eq, comparator_5_eq, comparator_6_eq, comparator_7_eq, comparator_8_eq,
       comparator_9_eq, comparator_10_eq, comparator_11_eq, comparator_12_eq, comparator_13_eq,
       comparator_14_eq, comparator_15_eq, comparator_16_eq, comparator_17_eq, comparator_18_eq,
       comparator_19_eq, comparator_20_eq, comparator_21_eq, comparator_22_eq, comparator_23_eq,
       comparator_24_eq, comparator_25_eq, comparator_26_eq, comparator_27_eq, comparator_28_eq,
       comparator_29_eq, comparator_30_eq, w;
  wire [15:10] register_1_q, register_2_q, register_3_q, register_4_q, register_5_q, register_6_q,
       register_7_q, register_8_q, register_9_q, register_10_q;
  wire [15:14] register_11_q, register_12_q, register_13_q, register_14_q, register_15_q, register_16_q,
       register_17_q, register_18_q, register_19_q, register_20_q;

  Comparator #(.width(16), .mode("unsigned")) comparator_1 (
    .a(in_1), .b(16'h8034), .eq(comparator_1_eq));  // open: gt, lt
  Comparator #(.width(16), .mode("unsigned")) comparator_2 (
    .a(in_1), .b(16'h8036), .eq(comparator_2_eq));  // open: gt, lt
  Comparator #(.width(16), .mode("unsigned")) comparator_3 (
    .a(in_1), .b(16'h8038), .eq(comparator_3_eq));  // open: gt, lt
  Comparator #(.width(16), .mode("unsigned")) comparator_4 (
    .a(in_1), .b(16'h803a), .eq(comparator_4_eq));  // open: gt, lt
  Comparator #(.width(16), .mode("unsigned")) comparator_5 (
    .a(in_1), .b(16'h803c), .eq(comparator_5_eq));  // open: gt, lt
  Comparator #(.width(16), .mode("unsigned")) comparator_6 (
    .a(in_1), .b(16'h803e), .eq(comparator_6_eq));  // open: gt, lt
  Comparator #(.width(16), .mode("unsigned")) comparator_7 (
    .a(in_1), .b(16'h8040), .eq(comparator_7_eq));  // open: gt, lt
  Comparator #(.width(16), .mode("unsigned")) comparator_8 (
    .a(in_1), .b(16'h8042), .eq(comparator_8_eq));  // open: gt, lt
  Comparator #(.width(16), .mode("unsigned")) comparator_9 (
    .a(in_1), .b(16'h8044), .eq(comparator_9_eq));  // open: gt, lt
  Comparator #(.width(16), .mode("unsigned")) comparator_10 (
    .a(in_1), .b(16'h8046), .eq(comparator_10_eq));  // open: gt, lt
  not not_1 (w, r_w_prime);
  and and_1 (and_1_out, comparator_1_eq, mem, w);
  and and_2 (and_2_out, comparator_2_eq, mem, w);
  and and_3 (and_3_out, comparator_3_eq, mem, w);
  and and_4 (and_4_out, comparator_4_eq, mem, w);
  and and_5 (and_5_out, comparator_5_eq, mem, w);
  and and_6 (and_6_out, comparator_6_eq, mem, w);
  and and_7 (and_7_out, comparator_7_eq, mem, w);
  and and_8 (and_8_out, comparator_8_eq, mem, w);
  and and_9 (and_9_out, comparator_9_eq, mem, w);
  and and_10 (and_10_out, comparator_10_eq, mem, w);
  Register #(.width(16), .trigger("falling")) register_1 (
    .D(data), .en(and_1_out), .Q({register_1_q, out1}), .clk(clk));  // open: clr
  Register #(.width(16), .trigger("falling")) register_2 (
    .D(data), .en(and_2_out), .Q({register_2_q, out2}), .clk(clk));  // open: clr
  Register #(.width(16), .trigger("falling")) register_3 (
    .D(data), .en(and_3_out), .Q({register_3_q, out3}), .clk(clk));  // open: clr
  Register #(.width(16), .trigger("falling")) register_4 (
    .D(data), .en(and_4_out), .Q({register_4_q, out4}), .clk(clk));  // open: clr
  Register #(.width(16), .trigger("falling")) register_5 (
    .D(data), .en(and_5_out), .Q({register_5_q, out5}), .clk(clk));  // open: clr
  Register #(.width(16), .trigger("falling")) register_6 (
    .D(data), .en(and_6_out), .Q({register_6_q, out6}), .clk(clk));  // open: clr
  Register #(.width(16), .trigger("falling")) register_7 (
    .D(data), .en(and_7_out), .Q({register_7_q, out7}), .clk(clk));  // open: clr
  Register #(.width(16), .trigger("falling")) register_8 (
    .D(data), .en(and_8_out), .Q({register_8_q, out8}), .clk(clk));  // open: clr
  Register #(.width(16), .trigger("falling")) register_9 (
    .D(data), .en(and_9_out), .Q({register_9_q, out9}), .clk(clk));  // open: clr
  Register #(.width(16), .trigger("falling")) register_10 (
    .D(data), .en(and_10_out), .Q({register_10_q, out10}), .clk(clk));  // open: clr
  Comparator #(.width(16), .mode("unsigned")) comparator_11 (
    .a(in_1), .b(16'h80a2), .eq(comparator_11_eq));  // open: gt, lt
  Comparator #(.width(16), .mode("unsigned")) comparator_12 (
    .a(in_1), .b(16'h80a4), .eq(comparator_12_eq));  // open: gt, lt
  Comparator #(.width(16), .mode("unsigned")) comparator_13 (
    .a(in_1), .b(16'h80a6), .eq(comparator_13_eq));  // open: gt, lt
  Comparator #(.width(16), .mode("unsigned")) comparator_14 (
    .a(in_1), .b(16'h80a8), .eq(comparator_14_eq));  // open: gt, lt
  Comparator #(.width(16), .mode("unsigned")) comparator_15 (
    .a(in_1), .b(16'h80aa), .eq(comparator_15_eq));  // open: gt, lt
  Comparator #(.width(16), .mode("unsigned")) comparator_16 (
    .a(in_1), .b(16'h80ac), .eq(comparator_16_eq));  // open: gt, lt
  Comparator #(.width(16), .mode("unsigned")) comparator_17 (
    .a(in_1), .b(16'h80ae), .eq(comparator_17_eq));  // open: gt, lt
  Comparator #(.width(16), .mode("unsigned")) comparator_18 (
    .a(in_1), .b(16'h80b0), .eq(comparator_18_eq));  // open: gt, lt
  Comparator #(.width(16), .mode("unsigned")) comparator_19 (
    .a(in_1), .b(16'h80b2), .eq(comparator_19_eq));  // open: gt, lt
  Comparator #(.width(16), .mode("unsigned")) comparator_20 (
    .a(in_1), .b(16'h80b4), .eq(comparator_20_eq));  // open: gt, lt
  and and_11 (and_11_out, comparator_11_eq, mem, w);
  and and_12 (and_12_out, comparator_12_eq, mem, w);
  and and_13 (and_13_out, comparator_13_eq, mem, w);
  and and_14 (and_14_out, comparator_14_eq, mem, w);
  and and_15 (and_15_out, comparator_15_eq, mem, w);
  and and_16 (and_16_out, comparator_16_eq, mem, w);
  and and_17 (and_17_out, comparator_17_eq, mem, w);
  and and_18 (and_18_out, comparator_18_eq, mem, w);
  and and_19 (and_19_out, comparator_19_eq, mem, w);
  and and_20 (and_20_out, comparator_20_eq, mem, w);
  Register #(.width(16), .trigger("falling")) register_11 (
    .D(data), .en(and_11_out), .Q({register_11_q, out1_3}), .clk(clk));  // open: clr
  Register #(.width(16), .trigger("falling")) register_12 (
    .D(data), .en(and_12_out), .Q({register_12_q, out2_3}), .clk(clk));  // open: clr
  Register #(.width(16), .trigger("falling")) register_13 (
    .D(data), .en(and_13_out), .Q({register_13_q, out3_3}), .clk(clk));  // open: clr
  Register #(.width(16), .trigger("falling")) register_14 (
    .D(data), .en(and_14_out), .Q({register_14_q, out4_3}), .clk(clk));  // open: clr
  Register #(.width(16), .trigger("falling")) register_15 (
    .D(data), .en(and_15_out), .Q({register_15_q, out5_3}), .clk(clk));  // open: clr
  Register #(.width(16), .trigger("falling")) register_16 (
    .D(data), .en(and_16_out), .Q({register_16_q, out6_3}), .clk(clk));  // open: clr
  Register #(.width(16), .trigger("falling")) register_17 (
    .D(data), .en(and_17_out), .Q({register_17_q, out7_3}), .clk(clk));  // open: clr
  Register #(.width(16), .trigger("falling")) register_18 (
    .D(data), .en(and_18_out), .Q({register_18_q, out8_3}), .clk(clk));  // open: clr
  Register #(.width(16), .trigger("falling")) register_19 (
    .D(data), .en(and_19_out), .Q({register_19_q, out9_3}), .clk(clk));  // open: clr
  Register #(.width(16), .trigger("falling")) register_20 (
    .D(data), .en(and_20_out), .Q({register_20_q, out10_3}), .clk(clk));  // open: clr
  Comparator #(.width(16), .mode("unsigned")) comparator_21 (
    .a(in_1), .b(16'h8086), .eq(comparator_21_eq));  // open: gt, lt
  Comparator #(.width(16), .mode("unsigned")) comparator_22 (
    .a(in_1), .b(16'h8088), .eq(comparator_22_eq));  // open: gt, lt
  Comparator #(.width(16), .mode("unsigned")) comparator_23 (
    .a(in_1), .b(16'h808a), .eq(comparator_23_eq));  // open: gt, lt
  Comparator #(.width(16), .mode("unsigned")) comparator_24 (
    .a(in_1), .b(16'h808c), .eq(comparator_24_eq));  // open: gt, lt
  Comparator #(.width(16), .mode("unsigned")) comparator_25 (
    .a(in_1), .b(16'h808e), .eq(comparator_25_eq));  // open: gt, lt
  Comparator #(.width(16), .mode("unsigned")) comparator_26 (
    .a(in_1), .b(16'h8090), .eq(comparator_26_eq));  // open: gt, lt
  Comparator #(.width(16), .mode("unsigned")) comparator_27 (
    .a(in_1), .b(16'h8092), .eq(comparator_27_eq));  // open: gt, lt
  Comparator #(.width(16), .mode("unsigned")) comparator_28 (
    .a(in_1), .b(16'h8094), .eq(comparator_28_eq));  // open: gt, lt
  Comparator #(.width(16), .mode("unsigned")) comparator_29 (
    .a(in_1), .b(16'h8096), .eq(comparator_29_eq));  // open: gt, lt
  Comparator #(.width(16), .mode("unsigned")) comparator_30 (
    .a(in_1), .b(16'h8098), .eq(comparator_30_eq));  // open: gt, lt
  Register #(.width(16), .trigger("falling")) register_21 (
    .D(data), .en(and_21_out), .Q(out1_2), .clk(clk));  // open: clr
  and and_21 (and_21_out, comparator_21_eq, mem, w);
  Register #(.width(16), .trigger("falling")) register_22 (
    .D(data), .en(and_22_out), .Q(out2_2), .clk(clk));  // open: clr
  and and_22 (and_22_out, comparator_22_eq, mem, w);
  Register #(.width(16), .trigger("falling")) register_23 (
    .D(data), .en(and_23_out), .Q(out3_2), .clk(clk));  // open: clr
  and and_23 (and_23_out, comparator_23_eq, mem, w);
  Register #(.width(16), .trigger("falling")) register_24 (
    .D(data), .en(and_24_out), .Q(out4_2), .clk(clk));  // open: clr
  and and_24 (and_24_out, comparator_24_eq, mem, w);
  Register #(.width(16), .trigger("falling")) register_25 (
    .D(data), .en(and_25_out), .Q(out5_2), .clk(clk));  // open: clr
  and and_25 (and_25_out, comparator_25_eq, mem, w);
  Register #(.width(16), .trigger("falling")) register_26 (
    .D(data), .en(and_26_out), .Q(out6_2), .clk(clk));  // open: clr
  and and_26 (and_26_out, comparator_26_eq, mem, w);
  Register #(.width(16), .trigger("falling")) register_27 (
    .D(data), .en(and_27_out), .Q(out7_2), .clk(clk));  // open: clr
  and and_27 (and_27_out, comparator_27_eq, mem, w);
  Register #(.width(16), .trigger("falling")) register_28 (
    .D(data), .en(and_28_out), .Q(out8_2), .clk(clk));  // open: clr
  and and_28 (and_28_out, comparator_28_eq, mem, w);
  Register #(.width(16), .trigger("falling")) register_29 (
    .D(data), .en(and_29_out), .Q(out9_2), .clk(clk));  // open: clr
  and and_29 (and_29_out, comparator_29_eq, mem, w);
  Register #(.width(16), .trigger("falling")) register_30 (
    .D(data), .en(and_30_out), .Q(out10_2), .clk(clk));  // open: clr
  and and_30 (and_30_out, comparator_30_eq, mem, w);

  // Other names for the same wires on the sheet: addr[15:0] = in_1
endmodule

module buttons (
  input  left,
  input  up,
  input  right,
  input  down,
  input  turn,
  input  fire_place,
  input  clk,
  output [15:0] out_8
);

  Register #(.width(16), .trigger("falling")) register_1 (
    .D({{10{1'b0}}, fire_place, turn, down, right, up, left}), .en(1'b1), .Q(out_8), .clk(clk));  // open: clr
endmodule

module front_detector (
  input  clk,
  input  button,
  output out_3
);

  wire register_1_q;

  Register #(.width(1)) register_1 (.D(button), .en(1'b1), .Q(register_1_q), .clk(clk));  // open: clr
  and and_1 (out_3, ~register_1_q, button);  // AND_Gate
endmodule
