// Logisim project project.circ as structural Verilog
// 🧻🧻
module main (
  output [15:0] out_1,
  output [15:0] out_2
);

  wire and_1_out, button_2_out, button_3_out, button_4_out, button_5_out, button_6_out, button_7_out,
       button_8_out, button_9_out, button_10_out, button_out, cdm_16_1_p3, clk, controller_tty_1_clr_tty,
       controller_tty_1_write_en_tty, io_off, mem, not_1_out, r_w_prime, word;
  wire [9:0] controller_bot_1_out1_3, controller_bot_1_out2_3, controller_bot_1_out3_3,
       controller_bot_1_out4_3, controller_bot_1_out5_3, controller_bot_1_out6_3, controller_bot_1_out7_3,
       controller_bot_1_out8_3, controller_bot_1_out9_3, controller_bot_1_out10_3, controller_gamer_1_out1_3,
       controller_gamer_1_out2_3, controller_gamer_1_out3_3, controller_gamer_1_out4_3,
       controller_gamer_1_out5_3, controller_gamer_1_out6_3, controller_gamer_1_out7_3,
       controller_gamer_1_out8_3, controller_gamer_1_out9_3, controller_gamer_1_out10_3;
  wire [13:0] controller_bot_1_out1_2, controller_bot_1_out2_2, controller_bot_1_out3_2,
       controller_bot_1_out4_2, controller_bot_1_out5_2, controller_bot_1_out6_2, controller_bot_1_out7_2,
       controller_bot_1_out8_2, controller_bot_1_out9_2, controller_bot_1_out10_2, controller_bot_1_out_23,
       controller_bot_1_out_24, controller_gamer_1_out1, controller_gamer_1_out2, controller_gamer_1_out3,
       controller_gamer_1_out4, controller_gamer_1_out5, controller_gamer_1_out6, controller_gamer_1_out7,
       controller_gamer_1_out8, controller_gamer_1_out9, controller_gamer_1_out10, controller_gamer_1_out_23,
       controller_gamer_1_out_24;
  wire [15:0] addr, controller_bot_1_out1, controller_bot_1_out2, controller_bot_1_out3,
       controller_bot_1_out4, controller_bot_1_out5, controller_bot_1_out6, controller_bot_1_out7,
       controller_bot_1_out8, controller_bot_1_out9, controller_bot_1_out10,
       controller_control_buttons_1_out_8, controller_gamer_1_out1_2, controller_gamer_1_out2_2,
       controller_gamer_1_out3_2, controller_gamer_1_out4_2, controller_gamer_1_out5_2,
       controller_gamer_1_out6_2, controller_gamer_1_out7_2, controller_gamer_1_out8_2,
       controller_gamer_1_out9_2, controller_gamer_1_out10_2, cotroller_draw_buttons_1_out_6, data, in, out;

  horizont_lines horizont_lines_1 ();
  controller_bot controller_bot_1 (
    .data(data), .in_1(addr), .mem(mem), .out1_2(controller_bot_1_out1_2), .out2_2(controller_bot_1_out2_2),
    .out3_2(controller_bot_1_out3_2), .out5_2(controller_bot_1_out5_2), .out6_2(controller_bot_1_out6_2),
    .out7_2(controller_bot_1_out7_2), .out10_2(controller_bot_1_out10_2), .out_23(controller_bot_1_out_23),
    .out_24(controller_bot_1_out_24), .out4_2(controller_bot_1_out4_2), .out8_2(controller_bot_1_out8_2),
    .out9_2(controller_bot_1_out9_2), .clk(clk), .r_w_prime(r_w_prime), .out1(controller_bot_1_out1),
    .out2(controller_bot_1_out2), .out3(controller_bot_1_out3), .out4(controller_bot_1_out4),
    .out5(controller_bot_1_out5), .out6(controller_bot_1_out6), .out7(controller_bot_1_out7),
    .out8(controller_bot_1_out8), .out9(controller_bot_1_out9), .out10(controller_bot_1_out10),
    .out1_3(controller_bot_1_out1_3), .out2_3(controller_bot_1_out2_3), .out3_3(controller_bot_1_out3_3),
    .out4_3(controller_bot_1_out4_3), .out5_3(controller_bot_1_out5_3), .out6_3(controller_bot_1_out6_3),
    .out7_3(controller_bot_1_out7_3), .out8_3(controller_bot_1_out8_3), .out9_3(controller_bot_1_out9_3),
    .out10_3(controller_bot_1_out10_3));
  horizont_lines horizont_lines_2 ();
  DotMatrix #(.inputtype("row"), .matrixcols(14), .matrixrows(12)) dotmatrix_1 (
    .row0(controller_bot_1_out_24), .row1(controller_bot_1_out_23), .row2(controller_bot_1_out1_2),
    .row3(controller_bot_1_out2_2), .row4(controller_bot_1_out3_2), .row5(controller_bot_1_out4_2),
    .row6(controller_bot_1_out5_2), .row7(controller_bot_1_out6_2), .row8(controller_bot_1_out7_2),
    .row9(controller_bot_1_out8_2), .row10(controller_bot_1_out9_2), .row11(controller_bot_1_out10_2));
  DotMatrix #(.inputtype("row"), .matrixcols(16), .matrixrows(10)) dotmatrix_2 (
    .row0(controller_bot_1_out1), .row1(controller_bot_1_out2), .row2(controller_bot_1_out3),
    .row3(controller_bot_1_out4), .row4(controller_bot_1_out5), .row5(controller_bot_1_out6),
    .row6(controller_bot_1_out7), .row7(controller_bot_1_out8), .row8(controller_bot_1_out9),
    .row9(controller_bot_1_out10));
  controller_tty controller_tty_1 (
    .mem(mem), .addr(addr), .write_en_tty(controller_tty_1_write_en_tty), .clr_tty(controller_tty_1_clr_tty),
    .r_w_prime(r_w_prime));
  DotMatrix #(.inputtype("row"), .matrixcols(10), .matrixrows(10)) dotmatrix_3 (
    .row0(controller_bot_1_out1_3), .row1(controller_bot_1_out2_3), .row2(controller_bot_1_out3_3),
    .row3(controller_bot_1_out4_3), .row4(controller_bot_1_out5_3), .row5(controller_bot_1_out6_3),
    .row6(controller_bot_1_out7_3), .row7(controller_bot_1_out8_3), .row8(controller_bot_1_out9_3),
    .row9(controller_bot_1_out10_3));
  Button button (.out(button_out));
  // Debugger debugger_1: pin names not known; wires that end beside it: out_2, 16'h100
  TTY #(.rows(3), .cols(50)) tty_1 (
    .data(data[6:0]), .clk(clk), .we(controller_tty_1_write_en_tty), .clr(controller_tty_1_clr_tty));
  cotroller_draw_buttons cotroller_draw_buttons_1 (
    .stone(button_3_out), .scissors(button_2_out), .paper(button_4_out), .clk(clk),
    .out_6(cotroller_draw_buttons_1_out_6), .confirm(button_out));
  Button button_2 (.out(button_2_out));
  Button button_3 (.out(button_3_out));
  controller_gamer controller_gamer_1 (
    .in_1(addr), .data(data), .clk(clk), .mem(mem), .r_w_prime(r_w_prime),
    .out_23(controller_gamer_1_out_23), .out_24(controller_gamer_1_out_24),
    .out1_2(controller_gamer_1_out1_2), .out2_2(controller_gamer_1_out2_2),
    .out3_2(controller_gamer_1_out3_2), .out4_2(controller_gamer_1_out4_2),
    .out5_2(controller_gamer_1_out5_2), .out6_2(controller_gamer_1_out6_2),
    .out7_2(controller_gamer_1_out7_2), .out8_2(controller_gamer_1_out8_2),
    .out9_2(controller_gamer_1_out9_2), .out10_2(controller_gamer_1_out10_2), .out1(controller_gamer_1_out1),
    .out2(controller_gamer_1_out2), .out3(controller_gamer_1_out3), .out4(controller_gamer_1_out4),
    .out5(controller_gamer_1_out5), .out6(controller_gamer_1_out6), .out7(controller_gamer_1_out7),
    .out8(controller_gamer_1_out8), .out9(controller_gamer_1_out9), .out10(controller_gamer_1_out10),
    .out1_3(controller_gamer_1_out1_3), .out2_3(controller_gamer_1_out2_3),
    .out3_3(controller_gamer_1_out3_3), .out4_3(controller_gamer_1_out4_3),
    .out5_3(controller_gamer_1_out5_3), .out6_3(controller_gamer_1_out6_3),
    .out7_3(controller_gamer_1_out7_3), .out8_3(controller_gamer_1_out8_3),
    .out9_3(controller_gamer_1_out9_3), .out10_3(controller_gamer_1_out10_3));
  DotMatrix #(.inputtype("row"), .matrixcols(14), .matrixrows(12)) dotmatrix_4 (
    .row0(controller_gamer_1_out_23), .row1(controller_gamer_1_out_24), .row2(controller_gamer_1_out1),
    .row3(controller_gamer_1_out2), .row4(controller_gamer_1_out3), .row5(controller_gamer_1_out4),
    .row6(controller_gamer_1_out5), .row7(controller_gamer_1_out6), .row8(controller_gamer_1_out7),
    .row9(controller_gamer_1_out8), .row10(controller_gamer_1_out9), .row11(controller_gamer_1_out10));
  DotMatrix #(.inputtype("row"), .matrixcols(10), .matrixrows(10)) dotmatrix_5 (
    .row0(controller_gamer_1_out1_3), .row1(controller_gamer_1_out2_3), .row2(controller_gamer_1_out3_3),
    .row3(controller_gamer_1_out4_3), .row4(controller_gamer_1_out5_3), .row5(controller_gamer_1_out6_3),
    .row6(controller_gamer_1_out7_3), .row7(controller_gamer_1_out8_3), .row8(controller_gamer_1_out9_3),
    .row9(controller_gamer_1_out10_3));
  DotMatrix #(.inputtype("row"), .matrixcols(16), .matrixrows(10)) dotmatrix_6 (
    .row0(controller_gamer_1_out1_2), .row1(controller_gamer_1_out2_2), .row2(controller_gamer_1_out3_2),
    .row3(controller_gamer_1_out4_2), .row4(controller_gamer_1_out5_2), .row5(controller_gamer_1_out6_2),
    .row6(controller_gamer_1_out7_2), .row7(controller_gamer_1_out8_2), .row8(controller_gamer_1_out9_2),
    .row9(controller_gamer_1_out10_2));
  Button button_4 (.out(button_4_out));
  Button button_5 (.out(button_5_out));
  Button button_6 (.out(button_6_out));
  Button button_7 (.out(button_7_out));
  controller_control_buttons controller_control_buttons_1 (
    .left(button_8_out), .up(button_6_out), .right(button_7_out), .down(button_9_out), .turn(button_5_out),
    .fire_place(button_10_out), .out_8(controller_control_buttons_1_out_8), .clk(clk));
  Button button_8 (.out(button_8_out));
  Button button_9 (.out(button_9_out));
  Button button_10 (.out(button_10_out));
  address_decoder_for_buttons_and_randgen address_decoder_for_buttons_and_randgen_1 (
    .r_w_prime(r_w_prime), .mem(mem), .addr(addr), .data_in(controller_control_buttons_1_out_8),
    .data_out_button(data), .clk(clk), .draw_button(cotroller_draw_buttons_1_out_6));
  // RAM ram_1: pin names not known; wires that end beside it: addr, word, io_off, clk, r_w_prime, data
  // CdM_16 cdm_16_1: pin names not known; wires that end beside it: clk, out_1, cdm_16_1_p3, cdm_16_1_p3, mem, r_w_prime, word, addr, out, in
  Clock clock_1 (.out(clk));
  assign data = not_1_out ? out : 16'bz;  // Controlled_Buffer controlled_buffer_1
  not not_1 (not_1_out, r_w_prime);
  assign in = r_w_prime ? data : 16'bz;  // Controlled_Buffer controlled_buffer_2
  and and_1 (and_1_out, addr[8], addr[9], addr[10], addr[11], addr[12], addr[13], addr[14], addr[15]);
  and and_2 (io_off, ~and_1_out, mem);  // AND_Gate

  // Other names for the same wires on the sheet: data0_6[6:0] = data[6:0]

  // Notes on the sheet:
  //   player matrix move - 0xff6a, hit- 0xff56, miss - 0xff40
  //   bot matrix  move - 0xff00, hit - 0xff14, miss - 0xff2a
  //   ENEMY FIELD
  //   PLAYER FIELD
  //   read button - 0xff80
  //   random - 0xff82
  //   wirte_to_tty - 0xffc0
  //   clear tty - 0xffc2
  //   8086 - hits
  //   805c - hits
  //   read draw button - 0xff84
  //   gamer - 8034 - move
  //   80a2 - missts
  //   bot - 8070 - move
  //   8016 - misses
endmodule

module controller_bot (
  input  [15:0] in_1,
  input  [15:0] data,
  input  clk,
  input  mem,
  input  r_w_prime,
  output [15:0] out1,
  output [15:0] out2,
  output [15:0] out3,
  output [15:0] out4,
  output [15:0] out5,
  output [15:0] out6,
  output [15:0] out7,
  output [15:0] out8,
  output [15:0] out9,
  output [15:0] out10,
  output [13:0] out1_2,
  output [13:0] out2_2,
  output [13:0] out3_2,
  output [13:0] out4_2,
  output [13:0] out5_2,
  output [13:0] out6_2,
  output [13:0] out7_2,
  output [13:0] out_23,
  output [13:0] out_24,
  output [13:0] out8_2,
  output [13:0] out9_2,
  output [13:0] out10_2,
  output [9:0] out1_3,
  output [9:0] out2_3,
  output [9:0] out3_3,
  output [9:0] out4_3,
  output [9:0] out5_3,
  output [9:0] out6_3,
  output [9:0] out7_3,
  output [9:0] out8_3,
  output [9:0] out9_3,
  output [9:0] out10_3
);

  wire address_decoder_for_bot_matrix_1_out_4, address_decoder_for_bot_matrix_1_out_5,
       address_decoder_for_bot_matrix_1_out_6, address_decoder_for_bot_matrix_1_out_7,
       address_decoder_for_bot_matrix_1_out_8, address_decoder_for_bot_matrix_1_out_9,
       address_decoder_for_bot_matrix_1_out_10, address_decoder_for_bot_matrix_1_out_11,
       address_decoder_for_bot_matrix_1_out_12, address_decoder_for_bot_matrix_1_out_13,
       address_decoder_for_bot_matrix_1_out_14, address_decoder_for_bot_matrix_1_out_15,
       address_decoder_for_bot_matrix_1_out_16, address_decoder_for_bot_matrix_1_out_17,
       address_decoder_for_bot_matrix_1_out_18, address_decoder_for_bot_matrix_1_out_19,
       address_decoder_for_bot_matrix_1_out_20, address_decoder_for_bot_matrix_1_out_21,
       address_decoder_for_bot_matrix_1_out_22, address_decoder_for_bot_matrix_1_out_23,
       address_decoder_for_bot_matrix_1_out_24, address_decoder_for_bot_matrix_1_out_25,
       address_decoder_for_bot_matrix_1_out_26, address_decoder_for_bot_matrix_1_out_27,
       address_decoder_for_bot_matrix_1_out_28, address_decoder_for_bot_matrix_1_out_29,
       address_decoder_for_bot_matrix_1_out_31, address_decoder_for_bot_matrix_1_out_33,
       address_decoder_for_bot_matrix_1_out_34, address_decoder_for_bot_matrix_1_out_35;
  wire [15:10] register_21_q, register_22_q, register_23_q, register_24_q, register_25_q, register_26_q,
       register_27_q, register_28_q, register_29_q, register_30_q;
  wire [15:14] register_11_q, register_12_q, register_13_q, register_14_q, register_15_q, register_16_q,
       register_17_q, register_18_q, register_19_q, register_20_q;

  address_decoder_for_bot_matrix address_decoder_for_bot_matrix_1 (
    .addr(in_1), .mem(mem), .out_4(address_decoder_for_bot_matrix_1_out_4),
    .out_5(address_decoder_for_bot_matrix_1_out_5), .out_6(address_decoder_for_bot_matrix_1_out_6),
    .out_7(address_decoder_for_bot_matrix_1_out_7), .out_8(address_decoder_for_bot_matrix_1_out_8),
    .out_9(address_decoder_for_bot_matrix_1_out_9), .out_10(address_decoder_for_bot_matrix_1_out_10),
    .out_11(address_decoder_for_bot_matrix_1_out_11), .out_12(address_decoder_for_bot_matrix_1_out_12),
    .out_13(address_decoder_for_bot_matrix_1_out_13), .out_14(address_decoder_for_bot_matrix_1_out_14),
    .out_15(address_decoder_for_bot_matrix_1_out_15), .out_16(address_decoder_for_bot_matrix_1_out_16),
    .out_17(address_decoder_for_bot_matrix_1_out_17), .out_18(address_decoder_for_bot_matrix_1_out_18),
    .out_19(address_decoder_for_bot_matrix_1_out_19), .out_20(address_decoder_for_bot_matrix_1_out_20),
    .out_21(address_decoder_for_bot_matrix_1_out_21), .out_22(address_decoder_for_bot_matrix_1_out_22),
    .out_23(address_decoder_for_bot_matrix_1_out_23), .out_24(address_decoder_for_bot_matrix_1_out_24),
    .out_25(address_decoder_for_bot_matrix_1_out_25), .out_26(address_decoder_for_bot_matrix_1_out_26),
    .out_27(address_decoder_for_bot_matrix_1_out_27), .out_28(address_decoder_for_bot_matrix_1_out_28),
    .out_29(address_decoder_for_bot_matrix_1_out_29), .out_31(address_decoder_for_bot_matrix_1_out_31),
    .out_33(address_decoder_for_bot_matrix_1_out_33), .out_34(address_decoder_for_bot_matrix_1_out_34),
    .r_w_prime(r_w_prime), .out_35(address_decoder_for_bot_matrix_1_out_35));  // open: io_en, io_off
  Register #(.width(16), .trigger("falling")) register_1 (
    .D(data), .en(address_decoder_for_bot_matrix_1_out_4), .Q(out1), .clk(clk));  // open: clr
  Register #(.width(16), .trigger("falling")) register_2 (
    .D(data), .en(address_decoder_for_bot_matrix_1_out_5), .Q(out2), .clk(clk));  // open: clr
  Register #(.width(16), .trigger("falling")) register_3 (
    .D(data), .en(address_decoder_for_bot_matrix_1_out_6), .Q(out3), .clk(clk));  // open: clr
  Register #(.width(16), .trigger("falling")) register_4 (
    .D(data), .en(address_decoder_for_bot_matrix_1_out_7), .Q(out4), .clk(clk));  // open: clr
  Register #(.width(16), .trigger("falling")) register_5 (
    .D(data), .en(address_decoder_for_bot_matrix_1_out_8), .Q(out5), .clk(clk));  // open: clr
  Register #(.width(16), .trigger("falling")) register_6 (
    .D(data), .en(address_decoder_for_bot_matrix_1_out_9), .Q(out6), .clk(clk));  // open: clr
  Register #(.width(16), .trigger("falling")) register_7 (
    .D(data), .en(address_decoder_for_bot_matrix_1_out_10), .Q(out7), .clk(clk));  // open: clr
  Register #(.width(16), .trigger("falling")) register_8 (
    .D(data), .en(address_decoder_for_bot_matrix_1_out_11), .Q(out8), .clk(clk));  // open: clr
  Register #(.width(16), .trigger("falling")) register_9 (
    .D(data), .en(address_decoder_for_bot_matrix_1_out_12), .Q(out9), .clk(clk));  // open: clr
  Register #(.width(16), .trigger("falling")) register_10 (
    .D(data), .en(address_decoder_for_bot_matrix_1_out_13), .Q(out10), .clk(clk));  // open: clr
  Register #(.width(16), .trigger("falling")) register_11 (
    .D(data), .en(address_decoder_for_bot_matrix_1_out_14), .Q({register_11_q, out1_2}), .clk(clk));  // open: clr
  Register #(.width(16), .trigger("falling")) register_12 (
    .D(data), .en(address_decoder_for_bot_matrix_1_out_15), .Q({register_12_q, out2_2}), .clk(clk));  // open: clr
  Register #(.width(16), .trigger("falling")) register_13 (
    .D(data), .en(address_decoder_for_bot_matrix_1_out_16), .Q({register_13_q, out3_2}), .clk(clk));  // open: clr
  Register #(.width(16), .trigger("falling")) register_14 (
    .D(data), .en(address_decoder_for_bot_matrix_1_out_17), .Q({register_14_q, out4_2}), .clk(clk));  // open: clr
  Register #(.width(16), .trigger("falling")) register_15 (
    .D(data), .en(address_decoder_for_bot_matrix_1_out_18), .Q({register_15_q, out5_2}), .clk(clk));  // open: clr
  Register #(.width(16), .trigger("falling")) register_16 (
    .D(data), .en(address_decoder_for_bot_matrix_1_out_19), .Q({register_16_q, out6_2}), .clk(clk));  // open: clr
  Register #(.width(16), .trigger("falling")) register_17 (
    .D(data), .en(address_decoder_for_bot_matrix_1_out_20), .Q({register_17_q, out7_2}), .clk(clk));  // open: clr
  Register #(.width(16), .trigger("falling")) register_18 (
    .D(data), .en(address_decoder_for_bot_matrix_1_out_21), .Q({register_18_q, out8_2}), .clk(clk));  // open: clr
  Register #(.width(16), .trigger("falling")) register_19 (
    .D(data), .en(address_decoder_for_bot_matrix_1_out_22), .Q({register_19_q, out9_2}), .clk(clk));  // open: clr
  Register #(.width(16), .trigger("falling")) register_20 (
    .D(data), .en(address_decoder_for_bot_matrix_1_out_23), .Q({register_20_q, out10_2}), .clk(clk));  // open: clr
  Register #(.width(16)) register_21 (
    .D(data), .en(address_decoder_for_bot_matrix_1_out_24), .Q({register_21_q, out1_3}), .clk(clk));  // open: clr
  Register #(.width(16)) register_22 (
    .D(data), .en(address_decoder_for_bot_matrix_1_out_25), .Q({register_22_q, out2_3}), .clk(clk));  // open: clr
  Register #(.width(16)) register_23 (
    .D(data), .en(address_decoder_for_bot_matrix_1_out_26), .Q({register_23_q, out3_3}), .clk(clk));  // open: clr
  Register #(.width(16)) register_24 (
    .D(data), .en(address_decoder_for_bot_matrix_1_out_27), .Q({register_24_q, out4_3}), .clk(clk));  // open: clr
  Register #(.width(16)) register_25 (
    .D(data), .en(address_decoder_for_bot_matrix_1_out_28), .Q({register_25_q, out5_3}), .clk(clk));  // open: clr
  Register #(.width(16)) register_26 (
    .D(data), .en(address_decoder_for_bot_matrix_1_out_29), .Q({register_26_q, out6_3}), .clk(clk));  // open: clr
  Register #(.width(16)) register_27 (
    .D(data), .en(address_decoder_for_bot_matrix_1_out_31), .Q({register_27_q, out7_3}), .clk(clk));  // open: clr
  Register #(.width(16)) register_28 (
    .D(data), .en(address_decoder_for_bot_matrix_1_out_33), .Q({register_28_q, out8_3}), .clk(clk));  // open: clr
  Register #(.width(16)) register_29 (
    .D(data), .en(address_decoder_for_bot_matrix_1_out_34), .Q({register_29_q, out9_3}), .clk(clk));  // open: clr
  Register #(.width(16)) register_30 (
    .D(data), .en(address_decoder_for_bot_matrix_1_out_35), .Q({register_30_q, out10_3}), .clk(clk));  // open: clr

  assign out_23 = {14{1'b0}};
  assign out_24 = {14{1'b0}};
endmodule

module controller_gamer (
  input  [15:0] in_1,
  input  [15:0] data,
  input  clk,
  input  mem,
  input  r_w_prime,
  output [13:0] out1,
  output [13:0] out2,
  output [13:0] out3,
  output [13:0] out4,
  output [13:0] out5,
  output [13:0] out6,
  output [13:0] out7,
  output [13:0] out8,
  output [13:0] out9,
  output [13:0] out10,
  output [15:0] out1_2,
  output [15:0] out2_2,
  output [15:0] out3_2,
  output [15:0] out4_2,
  output [15:0] out5_2,
  output [15:0] out6_2,
  output [15:0] out7_2,
  output [13:0] out_23,
  output [13:0] out_24,
  output [15:0] out8_2,
  output [15:0] out9_2,
  output [15:0] out10_2,
  output [9:0] out1_3,
  output [9:0] out2_3,
  output [9:0] out3_3,
  output [9:0] out4_3,
  output [9:0] out5_3,
  output [9:0] out6_3,
  output [9:0] out7_3,
  output [9:0] out8_3,
  output [9:0] out9_3,
  output [9:0] out10_3
);

  wire address_decoder_for_player_matrix_1_out_4, address_decoder_for_player_matrix_1_out_5,
       address_decoder_for_player_matrix_1_out_6, address_decoder_for_player_matrix_1_out_7,
       address_decoder_for_player_matrix_1_out_8, address_decoder_for_player_matrix_1_out_9,
       address_decoder_for_player_matrix_1_out_10, address_decoder_for_player_matrix_1_out_11,
       address_decoder_for_player_matrix_1_out_12, address_decoder_for_player_matrix_1_out_13,
       address_decoder_for_player_matrix_1_out_14, address_decoder_for_player_matrix_1_out_15,
       address_decoder_for_player_matrix_1_out_16, address_decoder_for_player_matrix_1_out_17,
       address_decoder_for_player_matrix_1_out_18, address_decoder_for_player_matrix_1_out_19,
       address_decoder_for_player_matrix_1_out_20, address_decoder_for_player_matrix_1_out_21,
       address_decoder_for_player_matrix_1_out_22, address_decoder_for_player_matrix_1_out_23,
       address_decoder_for_player_matrix_1_out_24, address_decoder_for_player_matrix_1_out_25,
       address_decoder_for_player_matrix_1_out_26, address_decoder_for_player_matrix_1_out_27,
       address_decoder_for_player_matrix_1_out_28, address_decoder_for_player_matrix_1_out_29,
       address_decoder_for_player_matrix_1_out_31, address_decoder_for_player_matrix_1_out_33,
       address_decoder_for_player_matrix_1_out_34, address_decoder_for_player_matrix_1_out_35;
  wire [15:10] register_21_q, register_22_q, register_23_q, register_24_q, register_25_q, register_26_q,
       register_27_q, register_28_q, register_29_q, register_30_q;
  wire [15:14] register_1_q, register_2_q, register_3_q, register_4_q, register_5_q, register_6_q,
       register_7_q, register_8_q, register_9_q, register_10_q;

  address_decoder_for_player_matrix address_decoder_for_player_matrix_1 (
    .r_w_prime(r_w_prime), .mem(mem), .addr(in_1), .out_4(address_decoder_for_player_matrix_1_out_4),
    .out_5(address_decoder_for_player_matrix_1_out_5), .out_6(address_decoder_for_player_matrix_1_out_6),
    .out_7(address_decoder_for_player_matrix_1_out_7), .out_8(address_decoder_for_player_matrix_1_out_8),
    .out_9(address_decoder_for_player_matrix_1_out_9), .out_10(address_decoder_for_player_matrix_1_out_10),
    .out_11(address_decoder_for_player_matrix_1_out_11), .out_12(address_decoder_for_player_matrix_1_out_12),
    .out_13(address_decoder_for_player_matrix_1_out_13), .out_14(address_decoder_for_player_matrix_1_out_14),
    .out_15(address_decoder_for_player_matrix_1_out_15), .out_16(address_decoder_for_player_matrix_1_out_16),
    .out_17(address_decoder_for_player_matrix_1_out_17), .out_18(address_decoder_for_player_matrix_1_out_18),
    .out_19(address_decoder_for_player_matrix_1_out_19), .out_20(address_decoder_for_player_matrix_1_out_20),
    .out_21(address_decoder_for_player_matrix_1_out_21), .out_22(address_decoder_for_player_matrix_1_out_22),
    .out_23(address_decoder_for_player_matrix_1_out_23), .out_24(address_decoder_for_player_matrix_1_out_24),
    .out_25(address_decoder_for_player_matrix_1_out_25), .out_26(address_decoder_for_player_matrix_1_out_26),
    .out_27(address_decoder_for_player_matrix_1_out_27), .out_28(address_decoder_for_player_matrix_1_out_28),
    .out_29(address_decoder_for_player_matrix_1_out_29), .out_31(address_decoder_for_player_matrix_1_out_31),
    .out_33(address_decoder_for_player_matrix_1_out_33), .out_34(address_decoder_for_player_matrix_1_out_34),
    .out_35(address_decoder_for_player_matrix_1_out_35));  // open: io_en, io_off
  Register #(.width(16), .trigger("falling")) register_1 (
    .D(data), .en(address_decoder_for_player_matrix_1_out_4), .Q({register_1_q, out1}), .clk(clk));  // open: clr
  Register #(.width(16), .trigger("falling")) register_2 (
    .D(data), .en(address_decoder_for_player_matrix_1_out_5), .Q({register_2_q, out2}), .clk(clk));  // open: clr
  Register #(.width(16), .trigger("falling")) register_3 (
    .D(data), .en(address_decoder_for_player_matrix_1_out_6), .Q({register_3_q, out3}), .clk(clk));  // open: clr
  Register #(.width(16), .trigger("falling")) register_4 (
    .D(data), .en(address_decoder_for_player_matrix_1_out_7), .Q({register_4_q, out4}), .clk(clk));  // open: clr
  Register #(.width(16), .trigger("falling")) register_5 (
    .D(data), .en(address_decoder_for_player_matrix_1_out_8), .Q({register_5_q, out5}), .clk(clk));  // open: clr
  Register #(.width(16), .trigger("falling")) register_6 (
    .D(data), .en(address_decoder_for_player_matrix_1_out_9), .Q({register_6_q, out6}), .clk(clk));  // open: clr
  Register #(.width(16), .trigger("falling")) register_7 (
    .D(data), .en(address_decoder_for_player_matrix_1_out_10), .Q({register_7_q, out7}), .clk(clk));  // open: clr
  Register #(.width(16), .trigger("falling")) register_8 (
    .D(data), .en(address_decoder_for_player_matrix_1_out_11), .Q({register_8_q, out8}), .clk(clk));  // open: clr
  Register #(.width(16), .trigger("falling")) register_9 (
    .D(data), .en(address_decoder_for_player_matrix_1_out_12), .Q({register_9_q, out9}), .clk(clk));  // open: clr
  Register #(.width(16), .trigger("falling")) register_10 (
    .D(data), .en(address_decoder_for_player_matrix_1_out_13), .Q({register_10_q, out10}), .clk(clk));  // open: clr
  Register #(.width(16), .trigger("falling")) register_11 (
    .D(data), .en(address_decoder_for_player_matrix_1_out_14), .Q(out1_2), .clk(clk));  // open: clr
  Register #(.width(16), .trigger("falling")) register_12 (
    .D(data), .en(address_decoder_for_player_matrix_1_out_15), .Q(out2_2), .clk(clk));  // open: clr
  Register #(.width(16), .trigger("falling")) register_13 (
    .D(data), .en(address_decoder_for_player_matrix_1_out_16), .Q(out3_2), .clk(clk));  // open: clr
  Register #(.width(16), .trigger("falling")) register_14 (
    .D(data), .en(address_decoder_for_player_matrix_1_out_17), .Q(out4_2), .clk(clk));  // open: clr
  Register #(.width(16), .trigger("falling")) register_15 (
    .D(data), .en(address_decoder_for_player_matrix_1_out_18), .Q(out5_2), .clk(clk));  // open: clr
  Register #(.width(16), .trigger("falling")) register_16 (
    .D(data), .en(address_decoder_for_player_matrix_1_out_19), .Q(out6_2), .clk(clk));  // open: clr
  Register #(.width(16), .trigger("falling")) register_17 (
    .D(data), .en(address_decoder_for_player_matrix_1_out_20), .Q(out7_2), .clk(clk));  // open: clr
  Register #(.width(16), .trigger("falling")) register_18 (
    .D(data), .en(address_decoder_for_player_matrix_1_out_21), .Q(out8_2), .clk(clk));  // open: clr
  Register #(.width(16), .trigger("falling")) register_19 (
    .D(data), .en(address_decoder_for_player_matrix_1_out_22), .Q(out9_2), .clk(clk));  // open: clr
  Register #(.width(16), .trigger("falling")) register_20 (
    .D(data), .en(address_decoder_for_player_matrix_1_out_23), .Q(out10_2), .clk(clk));  // open: clr
  Register #(.width(16)) register_21 (
    .D(data), .en(address_decoder_for_player_matrix_1_out_24), .Q({register_21_q, out1_3}), .clk(clk));  // open: clr
  Register #(.width(16)) register_22 (
    .D(data), .en(address_decoder_for_player_matrix_1_out_25), .Q({register_22_q, out2_3}), .clk(clk));  // open: clr
  Register #(.width(16)) register_23 (
    .D(data), .en(address_decoder_for_player_matrix_1_out_26), .Q({register_23_q, out3_3}), .clk(clk));  // open: clr
  Register #(.width(16)) register_24 (
    .D(data), .en(address_decoder_for_player_matrix_1_out_27), .Q({register_24_q, out4_3}), .clk(clk));  // open: clr
  Register #(.width(16)) register_25 (
    .D(data), .en(address_decoder_for_player_matrix_1_out_28), .Q({register_25_q, out5_3}), .clk(clk));  // open: clr
  Register #(.width(16)) register_26 (
    .D(data), .en(address_decoder_for_player_matrix_1_out_29), .Q({register_26_q, out6_3}), .clk(clk));  // open: clr
  Register #(.width(16)) register_27 (
    .D(data), .en(address_decoder_for_player_matrix_1_out_31), .Q({register_27_q, out7_3}), .clk(clk));  // open: clr
  Register #(.width(16)) register_28 (
    .D(data), .en(address_decoder_for_player_matrix_1_out_33), .Q({register_28_q, out8_3}), .clk(clk));  // open: clr
  Register #(.width(16)) register_29 (
    .D(data), .en(address_decoder_for_player_matrix_1_out_34), .Q({register_29_q, out9_3}), .clk(clk));  // open: clr
  Register #(.width(16)) register_30 (
    .D(data), .en(address_decoder_for_player_matrix_1_out_35), .Q({register_30_q, out10_3}), .clk(clk));  // open: clr

  assign out_23 = {14{1'b0}};
  assign out_24 = {14{1'b0}};
endmodule

module controller_control_buttons (
  input  left,
  input  up,
  input  right,
  input  down,
  input  turn,
  input  fire_place,
  input  clk,
  output [15:0] out_8
);

  Register #(.width(16), .trigger("falling")) register_1 (
    .D({{10{1'b0}}, fire_place, turn, down, right, up, left}), .en(1'b1), .Q(out_8), .clk(clk));  // open: clr
endmodule

module front_detector (
  input  clk,
  input  button,
  output out_3
);

  wire register_1_q;

  Register #(.width(1)) register_1 (.D(button), .en(1'b1), .Q(register_1_q), .clk(clk));  // open: clr
  and and_1 (out_3, ~register_1_q, button);  // AND_Gate
endmodule

module address_decoder_for_bot_matrix (
  input  r_w_prime,
  input  mem,
  input  [15:0] addr,
  output out_4,
  output out_5,
  output out_6,
  output out_7,
  output out_8,
  output out_9,
  output out_10,
  output out_11,
  output out_12,
  output out_13,
  output out_14,
  output out_15,
  output out_16,
  output out_17,
  output out_18,
  output out_19,
  output out_20,
  output out_21,
  output out_22,
  output out_23,
  output out_24,
  output out_25,
  output out_26,
  output out_27,
  output out_28,
  output out_29,
  output io_en,
  output out_31,
  output io_off,
  output out_33,
  output out_34,
  output out_35
);

  wire and_1_out, and_3_out, decoder_1_out0;

  and and_1 (and_1_out, addr[8], addr[9], addr[10], addr[11], addr[12], addr[13], addr[14], addr[15]);
  Decoder #(.select(2), .disabled(0)) decoder_1 (
    .out0(decoder_1_out0), .sel(addr[7:6]), .en(io_en));  // open: out1, out2, out3
  and and_2 (io_en, and_1_out, mem);
  Decoder #(.select(5), .disabled(0)) decoder_2 (
    .out0(out_4), .out1(out_5), .out2(out_6), .out3(out_7), .out4(out_8), .out5(out_9), .out6(out_10),
    .out7(out_11), .out8(out_12), .out9(out_13), .out10(out_14), .out11(out_15), .out12(out_16),
    .out13(out_17), .out14(out_18), .out15(out_19), .out16(out_20), .out17(out_21), .out18(out_22),
    .out19(out_23), .out21(out_24), .out22(out_25), .out23(out_26), .out24(out_27), .out25(out_28),
    .out26(out_29), .out27(out_31), .out28(out_33), .out29(out_34), .out30(out_35), .sel(addr[5:1]),
    .en(and_3_out));  // open: out20, out31
  and and_3 (and_3_out, ~r_w_prime, decoder_1_out0);  // AND_Gate
  not not_1 (io_off, io_en);
endmodule

module address_decoder_for_player_matrix (
  input  r_w_prime,
  input  mem,
  input  [15:0] addr,
  output out_4,
  output out_5,
  output out_6,
  output out_7,
  output out_8,
  output out_9,
  output out_10,
  output out_11,
  output out_12,
  output out_13,
  output out_14,
  output out_15,
  output out_16,
  output out_17,
  output out_18,
  output out_19,
  output out_20,
  output out_21,
  output out_22,
  output out_23,
  output out_24,
  output out_25,
  output out_26,
  output out_27,
  output out_28,
  output out_29,
  output io_en,
  output out_31,
  output io_off,
  output out_33,
  output out_34,
  output out_35
);

  wire and_1_out, and_3_out, decoder_1_out1;

  and and_1 (and_1_out, addr[8], addr[9], addr[10], addr[11], addr[12], addr[13], addr[14], addr[15]);
  Decoder #(.select(2), .disabled(0)) decoder_1 (
    .out1(decoder_1_out1), .sel(addr[7:6]), .en(io_en));  // open: out0, out2, out3
  and and_2 (io_en, and_1_out, mem);
  Decoder #(.select(5), .disabled(0)) decoder_2 (
    .out0(out_4), .out1(out_5), .out2(out_6), .out3(out_7), .out4(out_8), .out5(out_9), .out6(out_10),
    .out7(out_11), .out8(out_12), .out9(out_13), .out11(out_14), .out12(out_15), .out13(out_16),
    .out14(out_17), .out15(out_18), .out16(out_19), .out17(out_20), .out18(out_21), .out19(out_22),
    .out20(out_23), .out21(out_24), .out22(out_25), .out23(out_26), .out24(out_27), .out25(out_28),
    .out26(out_29), .out27(out_31), .out28(out_33), .out29(out_34), .out30(out_35), .sel(addr[5:1]),
    .en(and_3_out));  // open: out10, out31
  and and_3 (and_3_out, ~r_w_prime, decoder_1_out1);  // AND_Gate
  not not_1 (io_off, io_en);
endmodule

module address_decoder_for_buttons_and_randgen (
  input  [15:0] data_in,
  input  [15:0] draw_button,
  input  clk,
  input  r_w_prime,
  input  mem,
  input  [15:0] addr,
  output [15:0] data_out_button
);

  wire and_1_out, and_2_out, and_3_out, decoder_1_out2, decoder_2_out0, decoder_2_out1, decoder_2_out2,
       decoder_2_out3, decoder_2_out4, decoder_2_out5, decoder_2_out6, decoder_2_out7, decoder_2_out8,
       decoder_2_out9, decoder_2_out10, decoder_2_out11, decoder_2_out12, decoder_2_out13, decoder_2_out14,
       decoder_2_out15, decoder_2_out16, decoder_2_out17, decoder_2_out18, decoder_2_out19, decoder_2_out21,
       decoder_2_out22, decoder_2_out23, decoder_2_out24, decoder_2_out25, decoder_2_out26, decoder_2_out27,
       decoder_2_out28, decoder_2_out29, decoder_2_out30;
  wire [7:0] random_1_out;
  wire [15:0] bit_extender_1_out;

  and and_1 (and_1_out, addr[8], addr[9], addr[10], addr[11], addr[12], addr[13], addr[14], addr[15]);
  Decoder #(.select(2), .disabled(0)) decoder_1 (
    .out2(decoder_1_out2), .sel(addr[7:6]), .en(and_2_out));  // open: out0, out1, out3
  and and_2 (and_2_out, and_1_out, mem);
  Decoder #(.select(5), .disabled(0)) decoder_2 (
    .out0(decoder_2_out0), .out1(decoder_2_out1), .out2(decoder_2_out2), .out3(decoder_2_out3),
    .out4(decoder_2_out4), .out5(decoder_2_out5), .out6(decoder_2_out6), .out7(decoder_2_out7),
    .out8(decoder_2_out8), .out9(decoder_2_out9), .out10(decoder_2_out10), .out11(decoder_2_out11),
    .out12(decoder_2_out12), .out13(decoder_2_out13), .out14(decoder_2_out14), .out15(decoder_2_out15),
    .out16(decoder_2_out16), .out17(decoder_2_out17), .out18(decoder_2_out18), .out19(decoder_2_out19),
    .out21(decoder_2_out21), .out22(decoder_2_out22), .out23(decoder_2_out23), .out24(decoder_2_out24),
    .out25(decoder_2_out25), .out26(decoder_2_out26), .out27(decoder_2_out27), .out28(decoder_2_out28),
    .out29(decoder_2_out29), .out30(decoder_2_out30), .sel(addr[5:1]), .en(and_3_out));  // open: out20, out31
  and and_3 (and_3_out, r_w_prime, decoder_1_out2);
  assign data_out_button = decoder_2_out0 ? data_in : 16'bz;  // Controlled_Buffer controlled_buffer_1
  assign data_out_button = decoder_2_out2 ? draw_button : 16'bz;  // Controlled_Buffer controlled_buffer_2
  assign data_out_button = decoder_2_out1 ? bit_extender_1_out : 16'bz;  // Controlled_Buffer controlled_buffer_3
  Random random_1 (.clk(clk), .next(decoder_2_out1), .out(random_1_out));  // open: clr
  assign bit_extender_1_out = {{8{1'b0}}, random_1_out};  // Bit_Extender bit_extender_1
endmodule

module controller_tty (
  input  r_w_prime,
  input  mem,
  input  [15:0] addr,
  output write_en_tty,
  output clr_tty
);

  wire and_1_out, and_2_out, and_3_out, decoder_1_out3;

  and and_1 (and_1_out, addr[8], addr[9], addr[10], addr[11], addr[12], addr[13], addr[14], addr[15]);
  Decoder #(.select(2), .disabled(0)) decoder_1 (
    .out3(decoder_1_out3), .sel(addr[7:6]), .en(and_2_out));  // open: out0, out1, out2
  and and_2 (and_2_out, and_1_out, mem);
  Decoder #(.select(5), .disabled(0)) decoder_2 (
    .out0(write_en_tty), .out1(clr_tty), .sel(addr[5:1]), .en(and_3_out));  // open: out2, out3, out4, out5, out6, out7, out8, out9, out10, out11, out12, out13, out14, out15, out16, out17, out18, out19, out20, out21, out22, out23, out24, out25, out26, out27, out28, out29, out30, out31
  and and_3 (and_3_out, ~r_w_prime, decoder_1_out3);  // AND_Gate
endmodule

module cotroller_draw_buttons (
  input  stone,
  input  scissors,
  input  paper,
  input  confirm,
  input  clk,
  output [15:0] out_6
);

  Register #(.width(16), .trigger("falling")) register_1 (
    .D({{6{1'b0}}, confirm, paper, scissors, stone, {6{1'b0}}}), .en(1'b1), .Q(out_6), .clk(clk));  // open: clr
endmodule
